// Logisim project Project1.circ as structural Verilog: 7 circuits, main circuit main
module main (
  input  A,
  input  B,
  output W,
  output X,
  output D
);

  wire Clk, D2T_t, d2t_t_1_1_d2t_t_1, d_1_d, DR_t, dr_t_1_1_dr_t_1, DT_t, dt_t_1_1_dt_t___1, w_1_w, x_1_x;

  Clock clock_1 (.out(Clk));
  D d_1 (.A(A), .B(B), .D2T_t(D2T_t), .D(d_1_d));
  DT_t___1 dt_t_1_1 (.A(A), .B(B), .DT_t(DT_t), .DR_t(DR_t), .DT_t___1(dt_t_1_1_dt_t___1));
  DR_t___1 dr_t_1_1 (.A(A), .B(B), .DR_t(DR_t), .DT_t(DT_t), .D2T_t(D2T_t), .DR_t_1(dr_t_1_1_dr_t_1));
  W w_1 (.A(A), .B(B), .DT_t(DT_t), .D2T_t(D2T_t), .W(w_1_w));
  X x_1 (.A(A), .B(B), .DT_t(DT_t), .DR_t(DR_t), .D2T_t(D2T_t), .X(x_1_x));
  D_Flip_Flop d_ff_1 (.clk(Clk), .D(w_1_w), .Q(W));  // open: Qn, preset, en, reset
  D_Flip_Flop d_ff_2 (.clk(Clk), .D(x_1_x), .Q(X));  // open: Qn, preset, en, reset
  D_Flip_Flop d_ff_3 (.clk(Clk), .D(d_1_d), .Q(D));  // open: Qn, preset, en, reset
  D_Flip_Flop d_ff_4 (.clk(Clk), .D(dt_t_1_1_dt_t___1), .Q(DT_t));  // open: Qn, preset, en, reset
  D_Flip_Flop d_ff_5 (.clk(Clk), .D(dr_t_1_1_dr_t_1), .Q(DR_t));  // open: Qn, preset, en, reset
  D2T_t___1 d2t_t_1_1 (.A(A), .B(B), .DT_t(DT_t), .DR_t(DR_t), .D2T_t(D2T_t), .D2T_t_1(d2t_t_1_1_d2t_t_1));
  D_Flip_Flop d_ff_6 (.clk(Clk), .D(d2t_t_1_1_d2t_t_1), .Q(D2T_t));  // open: Qn, preset, en, reset
endmodule

module W (
  input  A,
  input  B,
  input  DT_t,
  input  D2T_t,
  output W
);

  wire and_1_out, and_2_out;

  and and_1 (and_1_out, A, B, DT_t);
  and and_2 (and_2_out, B, A, D2T_t);
  or or_1 (W, and_1_out, and_2_out);
endmodule

module X (
  input  A,
  input  B,
  input  DT_t,
  input  DR_t,
  input  D2T_t,
  output X
);

  wire and_1_out, and_2_out;

  and and_1 (and_1_out, A, B, D2T_t);
  and and_2 (and_2_out, B, A, DT_t, DR_t);
  or or_1 (X, and_1_out, and_2_out);
endmodule

module D (
  input  A,
  input  B,
  input  D2T_t,
  output D
);

  and and_1 (D, A, B, D2T_t);
endmodule

module DT_t___1 (
  input  A,
  input  B,
  input  DT_t,
  input  DR_t,
  output DT_t___1
);

  wire and_1_out, and_2_out, and_3_out, not_1_out, not_2_out;

  not not_1 (not_1_out, A);
  not not_2 (not_2_out, B);
  and and_1 (and_1_out, not_1_out, DT_t);
  and and_2 (and_2_out, A, not_2_out);
  and and_3 (and_3_out, B, not_1_out, DR_t);
  or or_1 (DT_t___1, and_1_out, and_2_out, and_3_out);
endmodule

module DR_t___1 (
  input  A,
  input  B,
  input  DR_t,
  input  DT_t,
  input  D2T_t,
  output DR_t_1
);

  wire and_1_out, and_2_out, and_3_out, not_1_out, not_2_out, not_3_out, not_4_out, not_5_out;

  not not_1 (not_1_out, B);
  not not_2 (not_2_out, DT_t);
  not not_3 (not_3_out, D2T_t);
  not not_4 (not_4_out, DR_t);
  not not_5 (not_5_out, A);
  and and_1 (and_1_out, not_1_out, DR_t);
  and and_2 (and_2_out, not_4_out, B, not_5_out);
  and and_3 (and_3_out, not_2_out, A, DR_t, not_3_out);
  or or_1 (DR_t_1, and_1_out, and_2_out, and_3_out);
endmodule

module D2T_t___1 (
  input  A,
  input  B,
  input  DT_t,
  input  DR_t,
  input  D2T_t,
  output D2T_t_1
);

  wire and_1_out, and_2_out, and_3_out, and_4_out, not_1_out, not_2_out;

  not not_1 (not_1_out, A);
  not not_2 (not_2_out, B);
  and and_1 (and_1_out, not_1_out, D2T_t);
  and and_2 (and_2_out, D2T_t, not_2_out);
  and and_3 (and_3_out, A, not_2_out, DT_t);
  and and_4 (and_4_out, not_1_out, B, DT_t, DR_t);
  or or_1 (D2T_t_1, and_1_out, and_2_out, and_3_out, and_4_out);
endmodule
